# Fritzing sketch rc522 (saved by Fritzing 0.9.3b)
breadboards: 2

parts:
  U2 = NodeMCU V1.0
  Bauteil1 = RFID-RC522-v3
  YwRobot_Power_Supply1 = YwRobot Breadboard Power Supply [part_number=545043]
  U3 = 2-Channel 5v Relay Shield [package=relay-2ch5v10a]
  R1 = Resistor [tolerance=±5% resistance=220 package="0805 [SMD]"]
  LED1 = RGB LED (com. anode, rbg) [package="5 mm [THT]"]
  R2 = Resistor [tolerance=±5% resistance=220 package="0805 [SMD]"]
  R3 = Resistor [tolerance=±5% resistance=220 package="0805 [SMD]"]

nets:
  N1: U2.D0, U3.IN1
  N2: U2.D1, Bauteil1.RST
  N3: U2.D2, R1.Pin_1
  N4: U2.D3, R3.Pin_1
  N5: U2.D4, R2.Pin_1
  GND: U2.GND, YwRobot_Power_Supply1.GND#13, YwRobot_Power_Supply1.GND#14, U3.GND, U3.IN2, LED1.blue_cathode
  N6: U2.D5, Bauteil1.SCK
  N7: U2.D6, Bauteil1.MISO
  N8: U2.D7, Bauteil1.MOSI
  N9: U2.D8, Bauteil1.SDA
  VIN: U2.Vin, YwRobot_Power_Supply1.VCC#9, YwRobot_Power_Supply1.VCC#10, U3.VCC
  N10: Bauteil1.GND, YwRobot_Power_Supply1.GND#11, YwRobot_Power_Supply1.GND#12
  N11: Bauteil1.3.3V, YwRobot_Power_Supply1.VCC#5, YwRobot_Power_Supply1.VCC#6
  N12: R1.Pin_0, LED1.red_cathode
  N13: LED1.common_anode, R3.Pin_0
  N14: LED1.green_cathode, R2.Pin_0

custom parts:
  NodeMCU V1.0: ESP8266 based NodeMCU
  RFID-RC522-v3: A simple China made RFID-RC522 Reader (6x4 cm); do check the pin labels, as this is a MFRC522 based clone.
  YwRobot Breadboard Power Supply: The YwRobot Breadboard Power Supply (MB-V2) has two power rails; they can be 5V or 3V3. Power to the module can be provided through the female USB socket or through the A10 (female) 2.1mm power jack.
  2-Channel 5v Relay Shield: 2 Channel 5v Relay Shield w. 2x SPD-06VDC-SD-C
